# Fritzing sketch matrix_circuit (saved by Fritzing 0.9.3b)
perfboards: 1

parts:
  Disp1 = LBT2088AH [part_number=LBT2088AH]
  Disp2 = LBT2088AH [part_number=LBT2088AH]
  パーツ1 = HT16K33 Breakout 16x8 LED Matrix Driver [part_number=1427]
  J1 = male pin header, 4 pins [form="♂ (male)"]

nets:
  N1: Disp1.pin1, Disp2.pin1, パーツ1.C4
  N2: Disp1.pin2, Disp2.pin2, パーツ1.C6
  N3: Disp1.pin_3, パーツ1.A1
  N4: Disp1.pin_4, パーツ1.A2
  N5: Disp1.pin_5, Disp2.pin_5, パーツ1.C7
  N6: Disp1.pin_6, パーツ1.A4
  N7: Disp1.pin_7, Disp2.pin_7, パーツ1.C5
  N8: Disp1.pin_8, Disp2.pin_8, パーツ1.C2
  N9: Disp1.pin_9, Disp2.pin_9, パーツ1.C0
  N10: Disp1.pin_10, パーツ1.A3
  N11: Disp1.pin_11, パーツ1.A5
  N12: Disp1.pin_12, Disp2.pin_12, パーツ1.C3
  N13: Disp1.pin_13, パーツ1.A0
  N14: Disp1.pin_14, Disp2.pin_14, パーツ1.C1
  N15: Disp1.pin_15, パーツ1.A6
  N16: Disp1.pin_16, パーツ1.A7
  N17: Disp2.pin_3, パーツ1.A9
  N18: Disp2.pin_4, パーツ1.A10
  N19: Disp2.pin_6, パーツ1.A12
  N20: Disp2.pin_10, パーツ1.A11
  N21: Disp2.pin_11, パーツ1.A13
  N22: Disp2.pin_13, パーツ1.A8
  N23: Disp2.pin_15, パーツ1.A14
  N24: Disp2.pin_16, パーツ1.A15
  SCL: パーツ1.SCL, J1.pin1
  SDA: パーツ1.SDA, J1.pin2
  5V: パーツ1.VDD, J1.pin4
  GND: パーツ1.GND, J1.pin3

custom parts:
  HT16K33 Breakout 16x8 LED Matrix Driver: This is the magic sauce in our 7-segment and matrix backpacks, now available in breadboard-friendly breakout board format. The HT16K33 is a neat little chip that has the ability to drive a multiplexed 16x8 matrix (that's 128 individual LEDs). The communication protocol is I2C so it uses only 2 pins, and you can have up to 8 selectable I2C addresses so thats a total of 8 matrices, each one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
